// Logisim project 74283icTEST.circ as structural Verilog: 2 circuits, main circuit main
module main (
);

  // DIP_74283 dip_74283_1: pin names not known
endmodule

module _74283ICtest (
  input  B3,
  input  B2,
  input  A3,
  input  A2,
  input  A4,
  input  A1,
  input  B4,
  input  B1,
  input  C0,
  output S2,
  output S3,
  output S1,
  output S4,
  output C4
);

  wire dip_74283_1_p1;

  // DIP_74283 dip_74283_1: pin names not known; wires that end beside it: dip_74283_1_p1, dip_74283_1_p1, S2, B2, A2, S1, A1, B1, C0, B3, A3, S3, A4, B4, S4, C4
endmodule
