// Logisim project AND-gate.circ as structural Verilog: 2 circuits, main circuit main
module main (
  input  in_1,
  input  in_2,
  output out_3
);

  // DIP_7408 dip_7408_1: pin names not known; wires that end beside it: in_1, in_2, out_3
endmodule

module AND_gate (
  input  in_1,
  input  in_2,
  output out_3
);

  // DIP_7408 dip_7408_1: pin names not known; wires that end beside it: in_1, in_2, out_3
endmodule
