# Fritzing sketch Untitled Sketch (saved by Fritzing 0.8.7b)
breadboards: 1

parts:
  YwRobot_Power_Supply1 = YwRobot Breadboard Power Supply [part_number=545043]
  R1 = Bussed Resistor-4 (SIP-5) [tolerance=±5% resistance=220 package=SIP-5]
  SW1 = DIP Switch 4 Position [package=dipswitch-04]
  IC1 = 74LS32 [chip_label=IC package="DIP (Dual Inline) [THT]"]
  IC1_PWR = 74LS32 [package="DIP (Dual Inline) [THT]"]  # not connected
  IC1_4 = 74LS32 [package="DIP (Dual Inline) [THT]"]  # not connected
  IC1_3 = 74LS32 [package="DIP (Dual Inline) [THT]"]  # not connected
  IC1_2 = 74LS32 [package="DIP (Dual Inline) [THT]"]  # not connected
  IC1_1 = 74LS32 [package="DIP (Dual Inline) [THT]"]  # not connected
  IC2 = 74LS32 [chip_label=IC package="DIP (Dual Inline) [THT]"]
  IC2_PWR = 74LS32 [package="DIP (Dual Inline) [THT]"]  # not connected
  IC2_4 = 74LS32 [package="DIP (Dual Inline) [THT]"]  # not connected
  IC2_3 = 74LS32 [package="DIP (Dual Inline) [THT]"]  # not connected
  IC2_2 = 74LS32 [package="DIP (Dual Inline) [THT]"]  # not connected
  IC2_1 = 74LS32 [package="DIP (Dual Inline) [THT]"]  # not connected
  SW2 = DIP Switch 4 Position [package=dipswitch-04]
  R2 = Bussed Resistor-4 (SIP-5) [tolerance=±5% resistance=220 package=SIP-5]

nets:
  N1: YwRobot_Power_Supply1.VCC#9, SW1.5, SW1.6, SW1.8, IC1.connector13, IC2.connector13
  N2: YwRobot_Power_Supply1.GND#11, R1.Pin_0, IC1.connector6, IC2.connector6, R2.Pin_0
  N3: R1.Pin_1, SW1.1, IC1.connector0, IC2.connector0
  N4: R1.Pin_2, SW1.2, IC1.connector1, IC2.connector1
  N5: R1.Pin_3, SW1.3
  N6: R1.Pin_4, SW1.4
  N7: IC1.connector2, SW2.8
  N8: IC2.connector2, SW2.7
  N9: SW2.1, R2.Pin_1
  N10: SW2.2, R2.Pin_2
  N11: SW2.3, R2.Pin_3
  N12: SW2.4, R2.Pin_4

custom parts:
  YwRobot Breadboard Power Supply: The YwRobot Breadboard Power Supply (MB-V2) has two power rails; they can be 5V or 3V3. Power to the module can be provided through the female USB socket or through the A10 (female) 2.1mm power jack.
  Bussed Resistor-4 (SIP-5): A resistor array is a single package which contains more than one resistor. They are typically used for convenience when several resistors are needed together in the same place in a circuit.
  74LS32: 2 input OR gate
  74LS32: 2 input OR gate
  74LS32: 2 input OR gate
  74LS32: 2 input OR gate
  74LS32: 2 input OR gate
  74LS32: 2 input OR gate
