// Logisim project 시험53.circ as structural Verilog
module exp_53 (
  input  A,
  input  B,
  input  Kn_1,
  output K,
  output D
);

  wire dip_7404_1_p2, dip_7404_1_p3, dip_7404_1_p4, dip_7408_1_p3, dip_7408_1_p6;

  // DIP_7404 dip_7404_1: pin names not known; wires that end beside it: A, dip_7404_1_p2, dip_7404_1_p3, dip_7404_1_p4
  // DIP_7408 dip_7408_1: pin names not known; wires that end beside it: dip_7404_1_p2, B, dip_7408_1_p3, dip_7404_1_p4, Kn_1, dip_7408_1_p6
  // DIP_7486 dip_7486_1: pin names not known; wires that end beside it: A, B, dip_7404_1_p3, dip_7404_1_p3, Kn_1, D
  // DIP_7432 dip_7432_1: pin names not known; wires that end beside it: dip_7408_1_p3, dip_7408_1_p6, K, K
endmodule
