// Logisim project Exer1-4.circ as structural Verilog
module AND_gate (
  output OUT,
  output A,
  output B
);

  // DIP_7408 dip_7408_1: pin names not known; wires that end beside it: A, B, OUT
endmodule

module OR_gate (
  input  B,
  output A,
  output OUT
);

  // DIP_7432 dip_7432_1: pin names not known; wires that end beside it: A, B, OUT
endmodule

module NAND_gate (
  input  OUT,
  input  B,
  output A
);

  // DIP_7400 dip_7400_1: pin names not known; wires that end beside it: A, B, OUT
endmodule

module NOR_gate (
  input  A,
  input  B,
  output OUT
);

  // DIP_7402 dip_7402_1: pin names not known; wires that end beside it: OUT, A, B
endmodule
